// Logisim project digital clock.circ as structural Verilog: 10 circuits, main circuit mod 10 decoder
module main (
);

  wire clock_1_out, hours_1_h1, hours_1_h2, hours_1_h3, hours_1_h4, hours_1_h5, hours_1_h6, hours_1_h7,
       hours_1_h8, minutes_1_m1, minutes_1_m2, minutes_1_m3, minutes_1_m4, minutes_1_m5, minutes_1_m6,
       minutes_1_m7, minutes_1_m8, mod_10_decoder_1_a_2, mod_10_decoder_1_b_2, mod_10_decoder_1_c_2,
       mod_10_decoder_1_d_2, mod_10_decoder_1_e, mod_10_decoder_1_f, mod_10_decoder_1_g,
       mod_10_decoder_2_a_2, mod_10_decoder_2_b_2, mod_10_decoder_2_c_2, mod_10_decoder_2_d_2,
       mod_10_decoder_2_e, mod_10_decoder_2_f, mod_10_decoder_2_g, mod_10_decoder_3_a_2,
       mod_10_decoder_3_b_2, mod_10_decoder_3_c_2, mod_10_decoder_3_d_2, mod_10_decoder_3_e,
       mod_10_decoder_3_f, mod_10_decoder_3_g, mod_10_decoder_4_a_2, mod_10_decoder_4_b_2,
       mod_10_decoder_4_c_2, mod_10_decoder_4_d_2, mod_10_decoder_4_e, mod_10_decoder_4_f,
       mod_10_decoder_4_g, mod_10_decoder_5_a_2, mod_10_decoder_5_b_2, mod_10_decoder_5_c_2,
       mod_10_decoder_5_d_2, mod_10_decoder_5_e, mod_10_decoder_5_f, mod_10_decoder_5_g,
       mod_10_decoder_6_a_2, mod_10_decoder_6_b_2, mod_10_decoder_6_c_2, mod_10_decoder_6_d_2,
       mod_10_decoder_6_e, mod_10_decoder_6_f, mod_10_decoder_6_g, seconds_1_s1, seconds_1_s2, seconds_1_s3,
       seconds_1_s4, seconds_1_s5, seconds_1_s6, seconds_1_s7, seconds_1_s8;

  Clock clock_1 (.out(clock_1_out));
  mod_10_decoder mod_10_decoder_1 (
    .A(hours_1_h5), .B(hours_1_h6), .C(hours_1_h7), .D(hours_1_h8), .a_2(mod_10_decoder_1_a_2),
    .b_2(mod_10_decoder_1_b_2), .c_2(mod_10_decoder_1_c_2), .d_2(mod_10_decoder_1_d_2),
    .e(mod_10_decoder_1_e), .f(mod_10_decoder_1_f), .g(mod_10_decoder_1_g));
  _7_Segment_Display u_7_segment_display_1 (
    .g(mod_10_decoder_1_g), .f(mod_10_decoder_1_f), .a(mod_10_decoder_1_a_2), .b(mod_10_decoder_1_b_2),
    .e(mod_10_decoder_1_e), .d(mod_10_decoder_1_d_2), .c(mod_10_decoder_1_c_2));  // open: dp
  _7_Segment_Display u_7_segment_display_2 (
    .g(mod_10_decoder_2_g), .f(mod_10_decoder_2_f), .a(mod_10_decoder_2_a_2), .b(mod_10_decoder_2_b_2),
    .e(mod_10_decoder_2_e), .d(mod_10_decoder_2_d_2), .c(mod_10_decoder_2_c_2));  // open: dp
  hours hours_1 (
    .clock(clock_1_out), .h8(hours_1_h8), .h7(hours_1_h7), .h6(hours_1_h6), .h5(hours_1_h5), .h4(hours_1_h4),
    .h3(hours_1_h3), .h2(hours_1_h2), .h1(hours_1_h1));
  mod_10_decoder mod_10_decoder_2 (
    .A(hours_1_h1), .B(hours_1_h2), .C(hours_1_h3), .D(hours_1_h4), .a_2(mod_10_decoder_2_a_2),
    .b_2(mod_10_decoder_2_b_2), .c_2(mod_10_decoder_2_c_2), .d_2(mod_10_decoder_2_d_2),
    .e(mod_10_decoder_2_e), .f(mod_10_decoder_2_f), .g(mod_10_decoder_2_g));
  _7_Segment_Display u_7_segment_display_3 (
    .g(mod_10_decoder_3_g), .f(mod_10_decoder_3_f), .a(mod_10_decoder_3_a_2), .b(mod_10_decoder_3_b_2),
    .e(mod_10_decoder_3_e), .d(mod_10_decoder_3_d_2), .c(mod_10_decoder_3_c_2));  // open: dp
  mod_10_decoder mod_10_decoder_3 (
    .A(minutes_1_m8), .B(minutes_1_m7), .C(minutes_1_m6), .D(minutes_1_m5), .a_2(mod_10_decoder_3_a_2),
    .b_2(mod_10_decoder_3_b_2), .c_2(mod_10_decoder_3_c_2), .d_2(mod_10_decoder_3_d_2),
    .e(mod_10_decoder_3_e), .f(mod_10_decoder_3_f), .g(mod_10_decoder_3_g));
  minutes minutes_1 (
    .clk(clock_1_out), .m8(minutes_1_m8), .m7(minutes_1_m7), .m6(minutes_1_m6), .m5(minutes_1_m5),
    .m4(minutes_1_m4), .m3(minutes_1_m3), .m2(minutes_1_m2), .m1(minutes_1_m1));
  _7_Segment_Display u_7_segment_display_4 (
    .g(mod_10_decoder_4_g), .f(mod_10_decoder_4_f), .a(mod_10_decoder_4_a_2), .b(mod_10_decoder_4_b_2),
    .e(mod_10_decoder_4_e), .d(mod_10_decoder_4_d_2), .c(mod_10_decoder_4_c_2));  // open: dp
  mod_10_decoder mod_10_decoder_4 (
    .A(minutes_1_m4), .B(minutes_1_m3), .C(minutes_1_m2), .D(minutes_1_m1), .a_2(mod_10_decoder_4_a_2),
    .b_2(mod_10_decoder_4_b_2), .c_2(mod_10_decoder_4_c_2), .d_2(mod_10_decoder_4_d_2),
    .e(mod_10_decoder_4_e), .f(mod_10_decoder_4_f), .g(mod_10_decoder_4_g));
  mod_10_decoder mod_10_decoder_5 (
    .A(seconds_1_s8), .B(seconds_1_s7), .C(seconds_1_s6), .D(seconds_1_s5), .a_2(mod_10_decoder_5_a_2),
    .b_2(mod_10_decoder_5_b_2), .c_2(mod_10_decoder_5_c_2), .d_2(mod_10_decoder_5_d_2),
    .e(mod_10_decoder_5_e), .f(mod_10_decoder_5_f), .g(mod_10_decoder_5_g));
  _7_Segment_Display u_7_segment_display_5 (
    .g(mod_10_decoder_6_g), .f(mod_10_decoder_6_f), .a(mod_10_decoder_6_a_2), .b(mod_10_decoder_6_b_2),
    .e(mod_10_decoder_6_e), .d(mod_10_decoder_6_d_2), .c(mod_10_decoder_6_c_2));  // open: dp
  _7_Segment_Display u_7_segment_display_6 (
    .g(mod_10_decoder_5_g), .f(mod_10_decoder_5_f), .a(mod_10_decoder_5_a_2), .b(mod_10_decoder_5_b_2),
    .e(mod_10_decoder_5_e), .d(mod_10_decoder_5_d_2), .c(mod_10_decoder_5_c_2));  // open: dp
  mod_10_decoder mod_10_decoder_6 (
    .A(seconds_1_s4), .B(seconds_1_s3), .C(seconds_1_s2), .D(seconds_1_s1), .a_2(mod_10_decoder_6_a_2),
    .b_2(mod_10_decoder_6_b_2), .c_2(mod_10_decoder_6_c_2), .d_2(mod_10_decoder_6_d_2),
    .e(mod_10_decoder_6_e), .f(mod_10_decoder_6_f), .g(mod_10_decoder_6_g));
  seconds seconds_1 (
    .clk(clock_1_out), .s8(seconds_1_s8), .s7(seconds_1_s7), .s6(seconds_1_s6), .s5(seconds_1_s5),
    .s4(seconds_1_s4), .s3(seconds_1_s3), .s2(seconds_1_s2), .s1(seconds_1_s1));
  _7_Segment_Display u_7_segment_display_7 (.g(1'b1), .f(1'b1), .b(1'b1), .e(1'b1), .c(1'b1));  // open: a, d, dp
  _7_Segment_Display u_7_segment_display_8 (.f(1'b1), .a(1'b1), .e(1'b1));  // open: g, b, d, c, dp
endmodule

module mod_10_decoder (
  input  A,
  input  B,
  input  C,
  input  D,
  output a_2,
  output b_2,
  output c_2,
  output d_2,
  output e,
  output f,
  output g
);

  wire and_1_out, and_2_out, and_3_out, and_4_out, and_5_out, and_6_out, and_7_out, and_8_out, and_9_out,
       and_10_out, and_11_out, and_12_out, and_13_out, and_14_out, and_15_out, and_16_out, not_1_out,
       not_2_out, not_3_out;

  not not_1 (not_1_out, B);
  not not_2 (not_2_out, C);
  not not_3 (not_3_out, D);
  and and_1 (and_1_out, not_1_out, not_3_out);
  and and_2 (and_2_out, B, D);
  and and_3 (and_3_out, not_2_out, not_3_out);
  and and_4 (and_4_out, C, D);
  or or_1 (c_2, not_2_out, D, B);
  and and_5 (and_5_out, not_1_out, not_3_out);
  and and_6 (and_6_out, not_1_out, C);
  and and_7 (and_7_out, C, not_3_out);
  and and_8 (and_8_out, B, not_2_out, D);
  and and_9 (and_9_out, not_1_out, not_3_out);
  and and_10 (and_10_out, C, not_3_out);
  and and_11 (and_11_out, not_2_out, not_3_out);
  and and_12 (and_12_out, B, not_2_out);
  and and_13 (and_13_out, B, not_3_out);
  and and_14 (and_14_out, not_1_out, C);
  and and_15 (and_15_out, C, not_3_out);
  and and_16 (and_16_out, B, not_2_out);
  or or_2 (a_2, A, and_1_out, C, and_2_out);
  or or_3 (b_2, and_3_out, and_4_out, not_1_out);
  or or_4 (d_2, and_5_out, A, and_6_out, and_7_out, and_8_out);
  or or_5 (e, and_9_out, and_10_out);
  or or_6 (f, and_11_out, and_12_out, and_13_out, A);
  or or_7 (g, A, and_14_out, and_15_out, and_16_out);
endmodule

module mod_10_counter (
  input  clk,
  input  en,
  output d1,
  output d2,
  output d3,
  output d4
);

  wire and_1_out, and_2_out, and_3_out, and_4_out, and_5_out, and_6_out, and_7_out, d1_qn, d2_qn, d3_qn,
       d_ff_1_qn, or_1_out, or_2_out, or_3_out;

  D_Flip_Flop u_d1 (.clk(clk), .D(d1_qn), .Q(d1), .Qn(d1_qn), .en(en));  // open: preset, reset
  and and_1 (and_1_out, d1, d_ff_1_qn, d2_qn);
  and and_2 (and_2_out, d1_qn, d2);
  or or_1 (or_1_out, and_1_out, and_2_out);
  D_Flip_Flop u_d2 (.clk(clk), .D(or_1_out), .Q(d2), .Qn(d2_qn), .en(en));  // open: preset, reset
  and and_3 (and_3_out, d3, d2_qn, d_ff_1_qn);
  and and_4 (and_4_out, d3, d2, d1_qn);
  and and_5 (and_5_out, d2, d1, d3_qn);
  or or_2 (or_2_out, and_3_out, and_4_out, and_5_out);
  D_Flip_Flop u_d3 (.clk(clk), .D(or_2_out), .Q(d3), .Qn(d3_qn), .en(en));  // open: preset, reset
  and and_6 (and_6_out, d2, d3, d1);
  and and_7 (and_7_out, d1_qn, d4);
  or or_3 (or_3_out, and_6_out, and_7_out);
  D_Flip_Flop d_ff_1 (.clk(clk), .D(or_3_out), .Q(d4), .Qn(d_ff_1_qn), .en(en));  // open: preset, reset
endmodule

module mod_6_decoder (
  input  A,
  input  B,
  input  C,
  output _1,
  output _2,
  output _3,
  output _4,
  output _5,
  output _6,
  output _7
);

  wire and_1_out, not_1_out, not_2_out, not_3_out, xnor_1_out;

  not not_1 (not_1_out, A);
  not not_2 (not_2_out, B);
  not not_3 (not_3_out, C);
  and and_1 (and_1_out, not_3_out, not_2_out);
  xnor xnor_1 (xnor_1_out, C, A);
  or or_1 (_1, xnor_1_out, B);
  or or_2 (_2, not_3_out, not_1_out);
  or or_3 (_3, A, not_2_out, C);
  or or_4 (_4, B, xnor_1_out);
  and and_2 (_5, not_1_out, not_3_out);
  or or_5 (_6, A, and_1_out);
  or or_6 (_7, A, B);
endmodule

module mod_6_counter (
  input  clk,
  input  in_2,
  output D1,
  output D2,
  output D3
);

  wire and_1_out, and_2_out, and_3_out, and_4_out, D1_qn, D2_qn, D3_qn, or_1_out, or_2_out;

  D_Flip_Flop u_D1 (.clk(clk), .D(D1_qn), .Q(D1), .Qn(D1_qn), .en(in_2));  // open: preset, reset
  D_Flip_Flop u_D2 (.clk(clk), .D(or_1_out), .Q(D2), .Qn(D2_qn), .en(in_2));  // open: preset, reset
  and and_1 (and_1_out, D1, D2_qn, D3_qn);
  or or_1 (or_1_out, and_1_out, and_2_out);
  and and_2 (and_2_out, D2, D1_qn);
  D_Flip_Flop u_D3 (.clk(clk), .D(or_2_out), .Q(D3), .Qn(D3_qn), .en(in_2));  // open: preset, reset
  and and_3 (and_3_out, D1, D2);
  or or_2 (or_2_out, and_3_out, and_4_out);
  and and_4 (and_4_out, D1_qn, D3);
endmodule

module seconds (
  input  clk,
  output s8,
  output s7,
  output s6,
  output s5,
  output s4,
  output s3,
  output s2,
  output s1
);

  wire and_1_out, not_1_out, not_2_out;

  mod_6_counter mod_6_counter_1 (.D1(s5), .D2(s6), .D3(s7), .clk(clk), .in_2(and_1_out));
  mod_10_counter mod_10_counter_1 (.d1(s1), .d2(s2), .d3(s3), .d4(s4), .clk(clk), .en(1'b1));
  and and_1 (and_1_out, s4, not_1_out, not_2_out, s1);
  not not_1 (not_1_out, s3);
  not not_2 (not_2_out, s2);

  assign s8 = 1'b0;
endmodule

module minutes (
  input  clk,
  output m8,
  output m7,
  output m4,
  output m3,
  output m2,
  output m6,
  output m1,
  output m5
);

  wire and_1_out, and_2_out, and_3_out, mod_6_counter_2_d1, mod_6_counter_2_d2, mod_6_counter_2_d3,
       mod_10_counter_2_d1, mod_10_counter_2_d2, mod_10_counter_2_d3, mod_10_counter_2_d4, not_1_out,
       not_2_out, not_3_out, not_4_out, not_5_out;

  mod_6_counter mod_6_counter_1 (.D1(m5), .D2(m6), .D3(m7), .clk(clk), .in_2(and_1_out));
  not not_1 (not_1_out, m3);
  not not_2 (not_2_out, m2);
  and and_1 (and_1_out, m1, not_2_out, not_1_out, m4, and_2_out);
  mod_10_counter mod_10_counter_1 (.d1(m1), .d2(m2), .d3(m3), .d4(m4), .clk(clk), .en(and_2_out));
  and and_2 (and_2_out, and_3_out, mod_6_counter_2_d1, not_3_out, mod_6_counter_2_d3);
  not not_3 (not_3_out, mod_6_counter_2_d2);
  mod_6_counter mod_6_counter_2 (
    .D1(mod_6_counter_2_d1), .D2(mod_6_counter_2_d2), .D3(mod_6_counter_2_d3), .clk(clk), .in_2(and_3_out));
  mod_10_counter mod_10_counter_2 (
    .d1(mod_10_counter_2_d1), .d2(mod_10_counter_2_d2), .d3(mod_10_counter_2_d3), .d4(mod_10_counter_2_d4),
    .clk(clk), .en(1'b1));
  and and_3 (and_3_out, mod_10_counter_2_d1, not_5_out, not_4_out, mod_10_counter_2_d4);
  not not_4 (not_4_out, mod_10_counter_2_d3);
  not not_5 (not_5_out, mod_10_counter_2_d2);

  assign m8 = 1'b0;
endmodule

module hours (
  input  clock,
  output h8,
  output h7,
  output h4,
  output h6,
  output h3,
  output h5,
  output h2,
  output h1
);

  wire and_1_out, and_2_out, and_3_out, and_4_out, mod_6_counter_1_d1, mod_6_counter_1_d2,
       mod_6_counter_1_d3, mod_6_counter_2_d1, mod_6_counter_2_d2, mod_6_counter_2_d3, mod_10_counter_1_d1,
       mod_10_counter_1_d2, mod_10_counter_1_d3, mod_10_counter_1_d4, mod_10_counter_2_d1,
       mod_10_counter_2_d2, mod_10_counter_2_d3, mod_10_counter_2_d4, mod_24_counter_1_d1,
       mod_24_counter_1_d2, mod_24_counter_1_d3, mod_24_counter_1_d4, mod_24_counter_1_d5, not_1_out,
       not_2_out, not_3_out, not_4_out, not_5_out, not_6_out;

  binary_to_bcd binary_to_bcd_1 (
    .d1(mod_24_counter_1_d1), .d2(mod_24_counter_1_d2), .d3(mod_24_counter_1_d3), .d4(mod_24_counter_1_d4),
    .d5(mod_24_counter_1_d5), .g1(h8), .g2(h7), .g3(h6), .g4(h5), .d1_2(h4), .d2_2(h3), .d3_2(h2), .d4_2(h1));
  mod_24_counter mod_24_counter_1 (
    .clock(clock), .d1(mod_24_counter_1_d1), .d2(mod_24_counter_1_d2), .d3(mod_24_counter_1_d3),
    .d4(mod_24_counter_1_d4), .d5(mod_24_counter_1_d5), .en(and_1_out));
  not not_1 (not_1_out, mod_6_counter_1_d2);
  and and_1 (and_1_out, mod_6_counter_1_d1, not_1_out, mod_6_counter_1_d3, and_2_out);
  mod_6_counter mod_6_counter_1 (
    .D1(mod_6_counter_1_d1), .D2(mod_6_counter_1_d2), .D3(mod_6_counter_1_d3), .clk(clock), .in_2(and_2_out));
  not not_2 (not_2_out, mod_10_counter_1_d3);
  not not_3 (not_3_out, mod_10_counter_1_d2);
  and and_2 (and_2_out, mod_10_counter_1_d1, not_3_out, not_2_out, mod_10_counter_1_d4, and_3_out);
  mod_10_counter mod_10_counter_1 (
    .d1(mod_10_counter_1_d1), .d2(mod_10_counter_1_d2), .d3(mod_10_counter_1_d3), .d4(mod_10_counter_1_d4),
    .clk(clock), .en(and_3_out));
  and and_3 (and_3_out, and_4_out, mod_6_counter_2_d1, not_4_out, mod_6_counter_2_d3);
  not not_4 (not_4_out, mod_6_counter_2_d2);
  mod_6_counter mod_6_counter_2 (
    .D1(mod_6_counter_2_d1), .D2(mod_6_counter_2_d2), .D3(mod_6_counter_2_d3), .clk(clock), .in_2(and_4_out));
  mod_10_counter mod_10_counter_2 (
    .d1(mod_10_counter_2_d1), .d2(mod_10_counter_2_d2), .d3(mod_10_counter_2_d3), .d4(mod_10_counter_2_d4),
    .clk(clock), .en(1'b1));
  and and_4 (and_4_out, mod_10_counter_2_d1, not_5_out, not_6_out, mod_10_counter_2_d4);
  not not_5 (not_5_out, mod_10_counter_2_d2);
  not not_6 (not_6_out, mod_10_counter_2_d3);
endmodule

module mod_24_counter (
  input  clock,
  input  en,
  output d1,
  output d2,
  output d3,
  output d4,
  output d5
);

  wire and_1_out, and_2_out, and_3_out, and_4_out, and_5_out, and_6_out, and_7_out, and_8_out, and_9_out,
       and_10_out, and_11_out, d_ff_1_qn, d_ff_2_qn, d_ff_3_qn, d_ff_4_qn, d_ff_5_qn, or_1_out, or_2_out,
       or_3_out, xor_1_out;

  D_Flip_Flop d_ff_1 (.clk(clock), .D(d_ff_1_qn), .Q(d1), .Qn(d_ff_1_qn), .en(en));  // open: preset, reset
  xor xor_1 (xor_1_out, d1, d2);
  D_Flip_Flop d_ff_2 (.clk(clock), .D(xor_1_out), .Q(d2), .Qn(d_ff_2_qn), .en(en));  // open: preset, reset
  D_Flip_Flop d_ff_3 (.clk(clock), .D(or_1_out), .Q(d3), .Qn(d_ff_3_qn), .en(en));  // open: preset, reset
  D_Flip_Flop d_ff_4 (.clk(clock), .D(or_2_out), .Q(d4), .Qn(d_ff_4_qn), .en(en));  // open: preset, reset
  D_Flip_Flop d_ff_5 (.clk(clock), .D(or_3_out), .Q(d5), .Qn(d_ff_5_qn), .en(en));  // open: preset, reset
  and and_1 (and_1_out, d_ff_2_qn, d3);
  and and_2 (and_2_out, d3, d_ff_1_qn);
  and and_3 (and_3_out, d_ff_3_qn, d4);
  and and_4 (and_4_out, d_ff_3_qn, d5);
  and and_5 (and_5_out, d1, d2, d_ff_3_qn);
  and and_6 (and_6_out, d4, d_ff_2_qn);
  and and_7 (and_7_out, d5, d_ff_2_qn);
  or or_1 (or_1_out, and_1_out, and_2_out, and_5_out);
  and and_8 (and_8_out, d4, d_ff_1_qn);
  and and_9 (and_9_out, d5, d_ff_1_qn);
  or or_2 (or_2_out, and_3_out, and_6_out, and_8_out, and_10_out);
  and and_10 (and_10_out, d1, d2, d3, d_ff_4_qn, d_ff_5_qn);
  and and_11 (and_11_out, d1, d2, d3, d4);
  or or_3 (or_3_out, and_4_out, and_7_out, and_9_out, and_11_out);
endmodule

module binary_to_bcd (
  input  d1,
  input  d2,
  input  d3,
  input  d4,
  input  d5,
  output g1,
  output g2,
  output g3,
  output g4,
  output d1_2,
  output d2_2,
  output d3_2,
  output d4_2
);

  wire and_1_out, and_2_out, and_3_out, and_5_out, and_6_out, and_7_out, and_8_out, and_9_out, and_10_out,
       and_11_out, and_12_out, and_13_out, not_1_out, not_2_out, not_3_out, not_4_out;

  not not_1 (not_1_out, d5);
  not not_2 (not_2_out, d2);
  not not_3 (not_3_out, d3);
  not not_4 (not_4_out, d4);
  and and_1 (and_1_out, d2, d4);
  and and_2 (and_2_out, d3, d4);
  and and_3 (and_3_out, not_3_out, d5);
  and and_4 (g2, d3, d5);
  and and_5 (and_5_out, not_1_out, not_4_out, d2);
  and and_6 (and_6_out, not_4_out, d3, d2);
  and and_7 (and_7_out, d4, d3, not_2_out);
  and and_8 (and_8_out, d5, not_3_out, not_2_out);
  and and_9 (and_9_out, not_1_out, not_4_out, d3);
  and and_10 (and_10_out, not_1_out, d3, d2);
  and and_11 (and_11_out, d5, not_3_out, not_2_out);
  and and_12 (and_12_out, d4, not_3_out, not_2_out);
  and and_13 (and_13_out, d5, not_3_out, d2);
  or or_1 (d4_2, and_12_out, and_13_out);
  or or_2 (g1, and_1_out, and_2_out, and_3_out);
  or or_3 (d2_2, and_5_out, and_6_out, and_7_out, and_8_out);
  or or_4 (d3_2, and_9_out, and_10_out, and_11_out);

  assign d1_2 = d1;
  assign g3 = 1'b0;
  assign g4 = 1'b0;
endmodule
